# Fritzing sketch Semaphore (saved by Fritzing 0.9.0b)
breadboards: 1

parts:
  Part1 = Arduino Leonardo (Rev3b)
  R1 = Resistor [tolerance=±5% resistance=330 package=THT]
  R2 = Resistor [tolerance=±5% resistance=330 package=THT]
  R3 = Resistor [tolerance=±5% resistance=330 package=THT]
  LED4 = LED - 5mm [color="Red (633nm)" package="5 mm [THT]"]
  LED5 = LED - 5mm [color="Yellow (592nm)" package="5 mm [THT]"]
  LED6 = LED - 5mm [color="Green (565nm)" package="5 mm [THT]"]

nets:
  N1: Part1.D5_PWM, R3.Pin_0
  N2: Part1.D7, R1.Pin_0
  N3: Part1.GND, LED4.anode, LED5.anode, LED6.anode
  N4: R1.Pin_1, LED4.cathode
  N5: R2.Pin_1, LED5.cathode
  N6: R3.Pin_1, LED6.cathode
